// Logisim project Computer_Architecture lab five.circ as structural Verilog: 1 circuit, main circuit main
module main (
  input  A,
  input  B,
  input  A_2,
  input  B_2,
  input  x,
  input  y,
  input  z,
  input  A_3,
  input  B_3,
  input  C
);

  wire and_1_out, and_2_out, and_3_out, and_4_out, and_5_out, and_6_out, and_7_out, and_8_out, and_9_out,
       nand_1_out, nand_2_out, nor_1_out, not_1_out, not_2_out, not_3_out, not_4_out, not_5_out, not_6_out,
       not_7_out, not_8_out, not_9_out, not_10_out, or_1_out, or_2_out, or_3_out, or_4_out, or_5_out;

  not not_1 (not_1_out, A_3);
  not not_2 (not_2_out, A);
  not not_3 (not_3_out, A_2);
  not not_4 (not_4_out, x);
  not not_5 (not_5_out, y);
  not not_6 (not_6_out, B_3);
  not not_7 (not_7_out, B);
  not not_8 (not_8_out, B_2);
  not not_9 (not_9_out, z);
  not not_10 (not_10_out, C);
  and and_1 (and_1_out, not_2_out, not_7_out);
  nand nand_1 (nand_1_out, A_2, B_2);
  or or_1 (or_1_out, not_3_out, not_8_out);
  nor nor_1 (nor_1_out, A, B);
  LED led_1 (.in(nor_1_out));
  LED led_2 (.in(and_1_out));
  LED led_3 (.in(nand_1_out));
  LED led_4 (.in(or_1_out));
  and and_2 (and_2_out, not_9_out, not_4_out);
  and and_3 (and_3_out, not_1_out, B_3, C);
  and and_4 (and_4_out, A_3, not_6_out, C);
  and and_5 (and_5_out, A_3, B_3, not_10_out);
  and and_6 (and_6_out, not_10_out, not_6_out, not_1_out);
  nand nand_2 (nand_2_out, z, y);
  and and_7 (and_7_out, y, x);
  and and_8 (and_8_out, y, not_4_out);
  or or_2 (or_2_out, x, and_2_out);
  and and_9 (and_9_out, x, nand_2_out);
  LED led_5 (.in(or_2_out));
  or or_3 (or_3_out, and_3_out, and_4_out, and_5_out, and_6_out);
  LED led_6 (.in(or_3_out));
  or or_4 (or_4_out, not_4_out, and_9_out);
  LED led_7 (.in(or_4_out));
  or or_5 (or_5_out, and_7_out, and_8_out);
  LED led_8 (.in(or_5_out));

  // Notes on the sheet:
  //   x
  //   A'
  //   A
  //   A'
  //   A
  //   B
  //   A'
  //   A
  //   x'
  //   y
  //   y'
  //   B
  //   B'
  //   C
  //   B'
  //   B
  //   B'
  //   z
  //   z'
  //   C'
  //   (A+B)'
  //   A'B'
  //   (AB)'
  //   A'+B'
  //   A’BC
  //   AB’C
  //   X = A'B'C' + AB'C + A'BC + ABC' 
  //   (yz)'
  //   xy
  //   x'y
  //   x'z'
  //   ABC’
  //   A'B'C' 
  //   (i)   (A + B)'  =   A . B 
  //   (ii ) A . B  =    A  + B 
  //   x(yz)'
  //    x+¯x.¯z
  //    x.¯("y.z" )+¯x
  //   ¯x y+"xz" 
  //   X = A'B'C' + AB'C + A'BC + ABC' 
endmodule
