// Logisim project lab6.circ as structural Verilog: 1 circuit, main circuit main
module main (
  input  A,
  input  B,
  input  A_2,
  input  B_2,
  input  Cin
);

  wire and_1_out, and_2_out, and_3_out, and_4_out, and_5_out, not_1_out, not_2_out, or_1_out, or_2_out,
       xor_1_out, xor_2_out;

  not not_1 (not_1_out, A);
  not not_2 (not_2_out, B);
  xor xor_1 (xor_1_out, A_2, B_2);
  and and_1 (and_1_out, not_1_out, B);
  and and_2 (and_2_out, A, not_2_out);
  and and_3 (and_3_out, A_2, B_2);
  or or_1 (or_1_out, and_1_out, and_2_out);
  and and_4 (and_4_out, A, B);
  xor xor_2 (xor_2_out, xor_1_out, Cin);
  and and_5 (and_5_out, xor_1_out, Cin);
  LED led_1 (.in(or_1_out));
  LED led_2 (.in(and_4_out));
  LED led_3 (.in(xor_2_out));
  or or_2 (or_2_out, and_5_out, and_3_out);
  LED led_4 (.in(or_2_out));

  // Notes on the sheet:
  //   A
  //   A
  //   A'
  //   B
  //   B
  //   B'
  //   A'B
  //   AB'
  //   A ⊕ B 
  //   A ⊕ B ⊕ Cin  
  //   A'B+AB'
  //   AB
endmodule
