// Logisim project ripple-burst.circ as structural Verilog: 1 circuit, main circuit main
module main (
  input  B3,
  input  A3,
  input  B2,
  input  A2,
  input  B1,
  input  A1,
  input  Cin,
  input  B0,
  input  A0
);

  wire and_1_out, and_2_out, and_3_out, and_4_out, and_5_out, and_6_out, and_7_out, and_8_out, or_1_out,
       or_2_out, or_3_out, or_4_out, xor_1_out, xor_2_out, xor_3_out, xor_4_out, xor_5_out, xor_6_out,
       xor_7_out, xor_8_out;

  and and_1 (and_1_out, or_2_out, xor_1_out);
  or or_1 (or_1_out, and_2_out, and_1_out);
  LED Cout (.in(or_1_out));
  and and_2 (and_2_out, A3, B3);
  xor xor_1 (xor_1_out, B3, A3);
  xor xor_2 (xor_2_out, or_2_out, xor_1_out);
  LED S3 (.in(xor_2_out));
  and and_3 (and_3_out, or_3_out, xor_3_out);
  or or_2 (or_2_out, and_4_out, and_3_out);
  and and_4 (and_4_out, A2, B2);
  xor xor_3 (xor_3_out, B2, A2);
  xor xor_4 (xor_4_out, or_3_out, xor_3_out);
  LED S2 (.in(xor_4_out));
  and and_5 (and_5_out, or_4_out, xor_5_out);
  or or_3 (or_3_out, and_6_out, and_5_out);
  and and_6 (and_6_out, A1, B1);
  xor xor_5 (xor_5_out, B1, A1);
  xor xor_6 (xor_6_out, or_4_out, xor_5_out);
  LED S1 (.in(xor_6_out));
  and and_7 (and_7_out, Cin, xor_7_out);
  or or_4 (or_4_out, and_8_out, and_7_out);
  and and_8 (and_8_out, A0, B0);
  xor xor_7 (xor_7_out, B0, A0);
  xor xor_8 (xor_8_out, Cin, xor_7_out);
  LED S0 (.in(xor_8_out));

  // Notes on the sheet:
  //   Carry 4
  //   Carry 3
  //   Carry 2
  //   Carry 1
  //   Input 
  //   output
  //   Sum 
endmodule
