// Logisim project lab9.circ as structural Verilog: 1 circuit, main circuit main
module main (
  input  in_1,
  input  D,
  input  E,
  input  [1:0] A_B,
  input  in_5,
  input  in_6,
  input  in_7,
  input  in_8,
  input  in_9,
  input  in_10,
  output out_11,
  output out_12,
  output out_13,
  output out_14,
  output out_15,
  output out_16,
  output out_17
);

  wire and_1_out, and_2_out, controlled_buffer_1_out, controlled_buffer_2_out, controlled_buffer_6_out,
       controlled_buffer_8_out, controlled_buffer_13_out, controlled_buffer_14_out, controlled_buffer_19_out,
       controlled_buffer_20_out, controlled_buffer_24_out, controlled_buffer_26_out, d_ff_1_q, d_ff_2_q,
       d_ff_3_q, d_ff_4_q, d_ff_5_q, d_ff_6_q, d_ff_7_q, d_ff_8_q, d_ff_9_q, d_ff_10_q, d_ff_11_q, d_ff_12_q,
       d_ff_13_q, d_ff_14_q, d_ff_15_q, d_ff_16_q, d_ff_17_q, d_ff_18_q, d_ff_19_q, d_ff_20_q,
       decoder_1_out0, decoder_1_out1, decoder_1_out2, decoder_1_out3, not_1_out, not_2_out, not_3_out,
       not_4_out, not_5_out, not_6_out, undriven;

  not not_1 (not_1_out, D);
  and and_1 (and_1_out, not_1_out, in_1);
  and and_2 (and_2_out, in_1, D);
  Decoder #(.select(2)) decoder_1 (
    .out0(decoder_1_out0), .out1(decoder_1_out1), .out2(decoder_1_out2), .out3(decoder_1_out3), .sel(A_B),
    .en(E));
  nor nor_1 (out_11, and_1_out, out_12);
  nor nor_2 (out_12, out_11, and_2_out);
  LED led_1 (.in(decoder_1_out0));
  LED led_2 (.in(decoder_1_out2));
  LED led_3 (.in(decoder_1_out3));
  assign controlled_buffer_1_out = not_2_out ? in_5 : 1'bz;  // Controlled_Buffer controlled_buffer_1
  not not_2 (not_2_out, in_10);
  LED led_4 (.in(out_11));
  LED led_5 (.in(out_12));
  LED led_6 (.in(decoder_1_out1));
  D_Flip_Flop #(.trigger("high")) d_ff_1 (
    .D(controlled_buffer_1_out), .clk(decoder_1_out0), .Q(d_ff_1_q));  // open: Qn, preset, reset
  D_Flip_Flop #(.trigger("high")) d_ff_2 (
    .D(controlled_buffer_1_out), .clk(decoder_1_out1), .Q(d_ff_2_q));  // open: Qn, preset, reset
  D_Flip_Flop #(.trigger("high")) d_ff_3 (
    .D(controlled_buffer_1_out), .clk(decoder_1_out2), .Q(d_ff_3_q));  // open: Qn, preset, reset
  D_Flip_Flop #(.trigger("high")) d_ff_4 (
    .D(controlled_buffer_1_out), .clk(decoder_1_out3), .Q(d_ff_4_q));  // open: Qn, preset, reset
  assign controlled_buffer_2_out = decoder_1_out0 ? d_ff_1_q : 1'bz;  // Controlled_Buffer controlled_buffer_2
  assign controlled_buffer_2_out = decoder_1_out1 ? d_ff_2_q : 1'bz;  // Controlled_Buffer controlled_buffer_3
  assign controlled_buffer_2_out = decoder_1_out2 ? d_ff_3_q : 1'bz;  // Controlled_Buffer controlled_buffer_4
  assign controlled_buffer_2_out = decoder_1_out3 ? d_ff_4_q : 1'bz;  // Controlled_Buffer controlled_buffer_5
  assign controlled_buffer_6_out = not_3_out ? in_6 : 1'bz;  // Controlled_Buffer controlled_buffer_6
  not not_3 (not_3_out, in_10);
  assign out_14 = in_10 ? controlled_buffer_2_out : 1'bz;  // Controlled_Buffer controlled_buffer_7
  LED led_7 (.in(out_14));
  D_Flip_Flop #(.trigger("high")) d_ff_5 (
    .D(controlled_buffer_6_out), .clk(decoder_1_out0), .Q(d_ff_5_q));  // open: Qn, preset, reset
  D_Flip_Flop #(.trigger("high")) d_ff_6 (
    .D(controlled_buffer_6_out), .clk(decoder_1_out1), .Q(d_ff_6_q));  // open: Qn, preset, reset
  D_Flip_Flop #(.trigger("high")) d_ff_7 (
    .D(controlled_buffer_6_out), .clk(decoder_1_out2), .Q(d_ff_7_q));  // open: Qn, preset, reset
  D_Flip_Flop #(.trigger("high")) d_ff_8 (
    .D(controlled_buffer_6_out), .clk(decoder_1_out3), .Q(d_ff_8_q));  // open: Qn, preset, reset
  assign controlled_buffer_8_out = decoder_1_out0 ? d_ff_5_q : 1'bz;  // Controlled_Buffer controlled_buffer_8
  assign controlled_buffer_8_out = decoder_1_out1 ? d_ff_6_q : 1'bz;  // Controlled_Buffer controlled_buffer_9
  assign controlled_buffer_8_out = decoder_1_out2 ? d_ff_7_q : 1'bz;  // Controlled_Buffer controlled_buffer_10
  assign controlled_buffer_8_out = decoder_1_out3 ? d_ff_8_q : 1'bz;  // Controlled_Buffer controlled_buffer_11
  assign out_15 = in_10 ? controlled_buffer_8_out : 1'bz;  // Controlled_Buffer controlled_buffer_12
  LED led_8 (.in(out_15));
  assign controlled_buffer_13_out = not_4_out ? in_7 : 1'bz;  // Controlled_Buffer controlled_buffer_13
  not not_4 (not_4_out, in_10);
  D_Flip_Flop #(.trigger("high")) d_ff_9 (.D(undriven), .clk(decoder_1_out0), .Q(d_ff_9_q));  // open: Qn, preset, reset
  assign controlled_buffer_14_out = decoder_1_out0 ? d_ff_9_q : 1'bz;  // Controlled_Buffer controlled_buffer_14
  D_Flip_Flop #(.trigger("high")) d_ff_10 (
    .D(undriven), .clk(decoder_1_out1), .Q(d_ff_10_q));  // open: Qn, preset, reset
  assign controlled_buffer_14_out = decoder_1_out1 ? d_ff_10_q : 1'bz;  // Controlled_Buffer controlled_buffer_15
  D_Flip_Flop #(.trigger("high")) d_ff_11 (
    .D(undriven), .clk(controlled_buffer_13_out), .Q(d_ff_11_q));  // open: Qn, preset, reset
  assign controlled_buffer_14_out = decoder_1_out2 ? d_ff_11_q : 1'bz;  // Controlled_Buffer controlled_buffer_16
  D_Flip_Flop #(.trigger("high")) d_ff_12 (
    .D(undriven), .clk(decoder_1_out3), .Q(d_ff_12_q));  // open: Qn, preset, reset
  assign controlled_buffer_14_out = decoder_1_out3 ? d_ff_12_q : 1'bz;  // Controlled_Buffer controlled_buffer_17
  assign out_16 = in_10 ? controlled_buffer_14_out : 1'bz;  // Controlled_Buffer controlled_buffer_18
  assign controlled_buffer_19_out = not_5_out ? in_8 : 1'bz;  // Controlled_Buffer controlled_buffer_19
  not not_5 (not_5_out, in_10);
  LED led_9 (.in(out_16));
  D_Flip_Flop #(.trigger("high")) d_ff_13 (
    .D(controlled_buffer_19_out), .clk(decoder_1_out0), .Q(d_ff_13_q));  // open: Qn, preset, reset
  D_Flip_Flop #(.trigger("high")) d_ff_14 (
    .D(controlled_buffer_19_out), .clk(decoder_1_out1), .Q(d_ff_14_q));  // open: Qn, preset, reset
  D_Flip_Flop #(.trigger("high")) d_ff_15 (
    .D(controlled_buffer_19_out), .clk(decoder_1_out2), .Q(d_ff_15_q));  // open: Qn, preset, reset
  D_Flip_Flop #(.trigger("high")) d_ff_16 (
    .D(controlled_buffer_19_out), .clk(decoder_1_out3), .Q(d_ff_16_q));  // open: Qn, preset, reset
  assign controlled_buffer_20_out = decoder_1_out0 ? d_ff_13_q : 1'bz;  // Controlled_Buffer controlled_buffer_20
  assign controlled_buffer_20_out = decoder_1_out1 ? d_ff_14_q : 1'bz;  // Controlled_Buffer controlled_buffer_21
  assign controlled_buffer_20_out = decoder_1_out2 ? d_ff_15_q : 1'bz;  // Controlled_Buffer controlled_buffer_22
  assign controlled_buffer_20_out = decoder_1_out3 ? d_ff_16_q : 1'bz;  // Controlled_Buffer controlled_buffer_23
  assign controlled_buffer_24_out = not_6_out ? in_9 : 1'bz;  // Controlled_Buffer controlled_buffer_24
  not not_6 (not_6_out, in_10);
  assign out_17 = in_10 ? controlled_buffer_20_out : 1'bz;  // Controlled_Buffer controlled_buffer_25
  LED led_10 (.in(out_17));
  D_Flip_Flop #(.trigger("high")) d_ff_17 (
    .D(controlled_buffer_24_out), .clk(decoder_1_out0), .Q(d_ff_17_q));  // open: Qn, preset, reset
  D_Flip_Flop #(.trigger("high")) d_ff_18 (
    .D(controlled_buffer_24_out), .clk(decoder_1_out1), .Q(d_ff_18_q));  // open: Qn, preset, reset
  D_Flip_Flop #(.trigger("high")) d_ff_19 (
    .D(controlled_buffer_24_out), .clk(decoder_1_out2), .Q(d_ff_19_q));  // open: Qn, preset, reset
  D_Flip_Flop #(.trigger("high")) d_ff_20 (
    .D(controlled_buffer_24_out), .clk(decoder_1_out3), .Q(d_ff_20_q));  // open: Qn, preset, reset
  assign controlled_buffer_26_out = decoder_1_out0 ? d_ff_17_q : 1'bz;  // Controlled_Buffer controlled_buffer_26
  assign controlled_buffer_26_out = decoder_1_out1 ? d_ff_18_q : 1'bz;  // Controlled_Buffer controlled_buffer_27
  assign controlled_buffer_26_out = decoder_1_out2 ? d_ff_19_q : 1'bz;  // Controlled_Buffer controlled_buffer_28
  assign controlled_buffer_26_out = decoder_1_out3 ? d_ff_20_q : 1'bz;  // Controlled_Buffer controlled_buffer_29
  assign out_13 = in_10 ? controlled_buffer_26_out : 1'bz;  // Controlled_Buffer controlled_buffer_30
  LED led_11 (.in(out_13));

  // Notes on the sheet:
  //   A, B  : address
  //         D2
  //   D3
  //   DI0
  //      D0
  //    D1
  //   Q
  //   Q'
  //   DI1
  //   Q1
  //   Q2
  //   Input : DI1,DI2,DI3,DI4
  //   DI2
  //   Q3
  //   Output : Q1,Q2,Q3,Q4,Q5 
  //       DI3
  //   DI4
  //   Q4
  //   Q5
endmodule
