// Logisim project lab08.circ as structural Verilog: 1 circuit, main circuit main
module main (
  input  X,
  input  Y,
  input  Z,
  input  A,
  input  B,
  input  C,
  input  D,
  input  X_2,
  input  Y_2,
  input  Z_2
);

  wire and_1_out, and_2_out, and_3_out, and_4_out, and_5_out, and_6_out, and_7_out, and_8_out, not_1_out,
       not_2_out, not_3_out, not_4_out, not_5_out, not_6_out, not_7_out, not_8_out, not_9_out, not_10_out,
       or_1_out, or_2_out, or_3_out;

  not not_1 (not_1_out, X);
  not not_2 (not_2_out, Y);
  not not_3 (not_3_out, A);
  not not_4 (not_4_out, X_2);
  not not_5 (not_5_out, Y_2);
  not not_6 (not_6_out, Z);
  not not_7 (not_7_out, B);
  not not_8 (not_8_out, C);
  not not_9 (not_9_out, Z_2);
  not not_10 (not_10_out, D);
  and and_1 (and_1_out, not_1_out, not_2_out);
  and and_2 (and_2_out, not_4_out, not_4_out);
  and and_3 (and_3_out, Y_2, Z_2);
  and and_4 (and_4_out, not_5_out, not_9_out);
  and and_5 (and_5_out, not_8_out, not_10_out);
  and and_6 (and_6_out, not_7_out, not_8_out);
  and and_7 (and_7_out, A, B);
  and and_8 (and_8_out, B, C, D);
  or or_1 (or_1_out, and_1_out, Z);
  LED led_1 (.in(or_1_out));
  or or_2 (or_2_out, and_2_out, and_3_out, and_4_out);
  LED led_2 (.in(or_2_out));
  or or_3 (or_3_out, and_5_out, and_6_out, and_7_out, and_8_out);
  LED led_3 (.in(or_3_out));

  // Notes on the sheet:
  //   X'
  //   Y'
  //   X'
  //   B'
  //   A'
  //   Y'
  //   Z'
  //   C'
  //   Z'
  //   D'
  //   Output 
  //   Output 
  //   Output 
endmodule
